# Fritzing sketch MFRC522 (saved by Fritzing 0.9.4)

parts:
  Componente1 = Arduino Mega ADK (Rev3)
  Componente2 = RFID-RC522-v2

nets:
  N1: Componente1.D13_PWM, Componente2.SCK
  N2: Componente1.D12_PWM, Componente2.MISO
  N3: Componente1.D11_PWM, Componente2.MOSI
  N4: Componente1.D10_PWM, Componente2.SDA
  N5: Componente1.D9_PWM, Componente2.RST
  3V3: Componente1.3V3, Componente2.3.3V
  GND: Componente1.GND, Componente2.GND

custom parts:
  RFID-RC522-v2: A simple China made RFID-RC522 Reader; do check the pin labels, as this is a MFRC522 based clone.
